// Logisim project Q4.circ as structural Verilog: 13 circuits, main circuit 1-bit Half Adder
module AND (
  input  A0,
  input  B0,
  input  A1,
  input  B1,
  input  A2,
  input  B2,
  input  A3,
  input  B3,
  output R0,
  output R1,
  output R2,
  output R3
);

  and and_1 (R0, A0, B0);
  and and_2 (R1, A1, B1);
  and and_3 (R2, A2, B2);
  and and_4 (R3, A3, B3);
endmodule

module OR (
  input  A0,
  input  B0,
  input  A1,
  input  B1,
  input  A2,
  input  B2,
  input  A3,
  input  B3,
  output R0,
  output R1,
  output R2,
  output R3
);

  or or_1 (R0, A0, B0);
  or or_2 (R1, A1, B1);
  or or_3 (R2, A2, B2);
  or or_4 (R3, A3, B3);
endmodule

module _4_bit_NOT (
  input  in_1,
  input  in_2,
  input  in_3,
  input  in_4,
  output out_5,
  output out_6,
  output out_7,
  output out_8
);

  not not_1 (out_5, in_1);
  not not_2 (out_6, in_2);
  not not_3 (out_7, in_3);
  not not_4 (out_8, in_4);
endmodule

module NOR (
  input  A0,
  input  B0,
  input  A1,
  input  B1,
  input  A2,
  input  B2,
  input  A3,
  input  B3,
  output R0,
  output R1,
  output R2,
  output R3
);

  wire OR_r0, OR_r1, OR_r2, OR_r3;

  OR OR (
    .A0(A0), .B0(B0), .A1(A1), .B1(B1), .A2(A2), .B2(B2), .A3(A3), .B3(B3), .R0(OR_r0), .R1(OR_r1),
    .R2(OR_r2), .R3(OR_r3));
  _4_bit_NOT NOT (
    .in_1(OR_r0), .in_2(OR_r1), .in_3(OR_r2), .in_4(OR_r3), .out_5(R0), .out_6(R1), .out_7(R2), .out_8(R3));
endmodule

module _1_bit_Half_Adder (
  input  A,
  input  B,
  output Sum,
  output Carry
);

  wire not_1_out, or_1_out;

  or or_1 (or_1_out, A, B);
  and and_1 (Carry, A, B);
  not not_1 (not_1_out, Carry);
  and and_2 (Sum, or_1_out, not_1_out);
endmodule

module _1_bit_Full_Adder (
  input  Carry_in,
  input  A,
  input  B,
  output Sum,
  output Carry_out
);

  wire n1_bit_half_adder_1_carry, n1_bit_half_adder_1_sum, n1_bit_half_adder_2_carry;

  _1_bit_Half_Adder u_1_bit_half_adder_1 (
    .A(A), .B(B), .Sum(n1_bit_half_adder_1_sum), .Carry(n1_bit_half_adder_1_carry));
  _1_bit_Half_Adder u_1_bit_half_adder_2 (
    .A(Carry_in), .B(n1_bit_half_adder_1_sum), .Sum(Sum), .Carry(n1_bit_half_adder_2_carry));
  or or_1 (Carry_out, n1_bit_half_adder_2_carry, n1_bit_half_adder_1_carry);
endmodule

module ADD (
  input  Zero,
  input  A0,
  input  B0,
  input  A1,
  input  B1,
  input  A2,
  input  B2,
  input  A3,
  input  B3,
  output R0,
  output R1,
  output R2,
  output R3,
  output Overflow
);

  wire n1_bit_full_adder_1_carry_out, n1_bit_full_adder_2_carry_out, n1_bit_full_adder_3_carry_out;

  _1_bit_Full_Adder u_1_bit_full_adder_1 (
    .Carry_in(Zero), .A(A0), .B(B0), .Sum(R0), .Carry_out(n1_bit_full_adder_1_carry_out));
  _1_bit_Full_Adder u_1_bit_full_adder_2 (
    .Carry_in(n1_bit_full_adder_1_carry_out), .A(A1), .B(B1), .Sum(R1),
    .Carry_out(n1_bit_full_adder_2_carry_out));
  _1_bit_Full_Adder u_1_bit_full_adder_3 (
    .Carry_in(n1_bit_full_adder_2_carry_out), .A(A2), .B(B2), .Sum(R2),
    .Carry_out(n1_bit_full_adder_3_carry_out));
  _1_bit_Full_Adder u_1_bit_full_adder_4 (
    .Carry_in(n1_bit_full_adder_3_carry_out), .A(A3), .B(B3), .Sum(R3), .Carry_out(Overflow));
endmodule

module SUB (
  input  Carry_in_Should_be_1,
  input  A0,
  input  B0,
  input  A1,
  input  B1,
  input  A2,
  input  B2,
  input  A3,
  input  B3,
  output R0,
  output R1,
  output R2,
  output R3,
  output Overflow
);

  wire n1_bit_full_adder_1_carry_out, n1_bit_full_adder_2_carry_out, n1_bit_full_adder_3_carry_out,
       n1_bit_full_adder_4_carry_out, not_1_out, not_2_out, not_3_out, not_4_out;

  not not_1 (not_1_out, B0);
  not not_2 (not_2_out, B1);
  not not_3 (not_3_out, B2);
  not not_4 (not_4_out, B3);
  _1_bit_Full_Adder u_1_bit_full_adder_1 (
    .Carry_in(Carry_in_Should_be_1), .A(A0), .B(not_1_out), .Sum(R0),
    .Carry_out(n1_bit_full_adder_1_carry_out));
  _1_bit_Full_Adder u_1_bit_full_adder_2 (
    .Carry_in(n1_bit_full_adder_1_carry_out), .A(A1), .B(not_2_out), .Sum(R1),
    .Carry_out(n1_bit_full_adder_2_carry_out));
  _1_bit_Full_Adder u_1_bit_full_adder_3 (
    .Carry_in(n1_bit_full_adder_2_carry_out), .A(A2), .B(not_3_out), .Sum(R2),
    .Carry_out(n1_bit_full_adder_3_carry_out));
  _1_bit_Full_Adder u_1_bit_full_adder_4 (
    .Carry_in(n1_bit_full_adder_3_carry_out), .A(A3), .B(not_4_out), .Sum(R3),
    .Carry_out(n1_bit_full_adder_4_carry_out));
  xor xor_1 (Overflow, n1_bit_full_adder_3_carry_out, n1_bit_full_adder_4_carry_out);
endmodule

module SLT (
  input  A0,
  input  B0,
  input  Should_be_1,
  input  A1,
  input  B1,
  input  A2,
  input  B2,
  input  A3,
  input  B3,
  output R0,
  output R1,
  output R2,
  output R3
);

  wire and_1_out, and_2_out, and_3_out, not_2_out, not_3_out, sub_1_r3;

  SUB sub_1 (
    .A0(A0), .B0(B0), .A1(A1), .B1(B1), .A2(A2), .B2(B2), .A3(A3), .B3(B3),
    .Carry_in_Should_be_1(Should_be_1), .R3(sub_1_r3));  // open: R0, R1, R2, Overflow
  not not_1 (R1, Should_be_1);
  not not_2 (not_2_out, B3);
  not not_3 (not_3_out, B3);
  and and_1 (and_1_out, not_2_out, sub_1_r3);
  or or_1 (R0, and_1_out, and_2_out, and_3_out);
  and and_2 (and_2_out, A3, not_3_out);
  and and_3 (and_3_out, A3, sub_1_r3);

  assign R2 = R1;
  assign R3 = R1;
endmodule

module Decoder (
  input  C0,
  input  C1,
  input  C2,
  input  C3,
  output r0,
  output r1,
  output r2,
  output r3,
  output r4,
  output r5
);

  wire not_1_out, not_2_out, not_3_out, not_4_out, not_5_out, not_6_out, not_7_out;

  not not_1 (not_1_out, C0);
  and and_1 (r0, not_1_out, not_2_out, not_3_out);
  not not_2 (not_2_out, C1);
  not not_3 (not_3_out, C2);
  and and_2 (r1, C0, not_4_out);
  not not_4 (not_4_out, C1);
  and and_3 (r2, C1, not_5_out);
  not not_5 (not_5_out, C2);
  not not_6 (not_6_out, C0);
  and and_4 (r3, not_6_out, C2, not_7_out);
  not not_7 (not_7_out, C3);
  and and_5 (r4, C0, C2);

  assign r5 = C3;
endmodule

module _6_to_1_multiplexer (
  input  C3,
  input  C2,
  input  C1,
  input  C0,
  input  _0,
  input  _1,
  input  _2,
  input  _3,
  input  _4,
  input  _5,
  output R
);

  wire and_1_out, and_2_out, and_3_out, and_4_out, and_5_out, and_6_out, Decoder_r0, Decoder_r1, Decoder_r2,
       Decoder_r3, Decoder_r4, Decoder_r5;

  Decoder Decoder (
    .C0(C0), .C1(C1), .C2(C2), .C3(C3), .r0(Decoder_r0), .r1(Decoder_r1), .r2(Decoder_r2), .r3(Decoder_r3),
    .r4(Decoder_r4), .r5(Decoder_r5));
  and and_1 (and_1_out, _0, Decoder_r0);
  and and_2 (and_2_out, _1, Decoder_r1);
  and and_3 (and_3_out, _2, Decoder_r2);
  and and_4 (and_4_out, _3, Decoder_r3);
  and and_5 (and_5_out, _4, Decoder_r4);
  and and_6 (and_6_out, _5, Decoder_r5);
  or or_1 (R, and_3_out, and_1_out, and_2_out, and_4_out, and_5_out, and_6_out);
endmodule

module ALU (
  input  C0,
  input  C1,
  input  C2,
  input  C3,
  input  Should_stay_Zero,
  input  A0,
  input  B0,
  input  A1,
  input  B1,
  input  A2,
  input  B2,
  input  A3,
  input  B3,
  output R0,
  output R1,
  output R2,
  output R3,
  output OVERFLOW,
  output ZERO
);

  wire ADD_overflow, ADD_r0, ADD_r1, ADD_r2, ADD_r3, AND_r0, AND_r1, AND_r2, AND_r3, NOR_r0, NOR_r1, NOR_r2,
       NOR_r3, not_1_out, not_2_out, not_3_out, not_4_out, not_5_out, OR_r0, OR_r1, OR_r2, OR_r3, SLT_r0,
       SLT_r1, SLT_r2, SLT_r3, SUB_overflow, SUB_r0, SUB_r1, SUB_r2, SUB_r3;

  not not_1 (not_1_out, Should_stay_Zero);
  AND AND (
    .A0(A0), .B0(B0), .A1(A1), .B1(B1), .A2(A2), .B2(B2), .A3(A3), .B3(B3), .R0(AND_r0), .R1(AND_r1),
    .R2(AND_r2), .R3(AND_r3));
  OR OR (
    .A0(A0), .B0(B0), .A1(A1), .B1(B1), .A2(A2), .B2(B2), .A3(A3), .B3(B3), .R0(OR_r0), .R1(OR_r1),
    .R2(OR_r2), .R3(OR_r3));
  ADD ADD (
    .A0(A0), .B0(B0), .A1(A1), .B1(B1), .A2(A2), .B2(B2), .A3(A3), .B3(B3), .R0(ADD_r0), .R1(ADD_r1),
    .R2(ADD_r2), .R3(ADD_r3), .Zero(Should_stay_Zero), .Overflow(ADD_overflow));
  SUB SUB (
    .A0(A0), .B0(B0), .A1(A1), .B1(B1), .A2(A2), .B2(B2), .A3(A3), .B3(B3), .Carry_in_Should_be_1(not_1_out),
    .R0(SUB_r0), .R1(SUB_r1), .R2(SUB_r2), .R3(SUB_r3), .Overflow(SUB_overflow));
  SLT SLT (
    .A0(A0), .B0(B0), .A1(A1), .B1(B1), .A2(A2), .B2(B2), .A3(A3), .B3(B3), .Should_be_1(not_1_out),
    .R0(SLT_r0), .R1(SLT_r1), .R2(SLT_r2), .R3(SLT_r3));
  NOR NOR (
    .A0(A0), .B0(B0), .A1(A1), .B1(B1), .A2(A2), .B2(B2), .A3(A3), .B3(B3), .R0(NOR_r0), .R1(NOR_r1),
    .R2(NOR_r2), .R3(NOR_r3));
  _6_to_1_multiplexer u_R0 (
    ._0(AND_r0), ._1(OR_r0), ._2(ADD_r0), ._3(SUB_r0), ._4(SLT_r0), ._5(NOR_r0), .R(R0), .C3(C3), .C2(C2),
    .C1(C1), .C0(C0));
  _6_to_1_multiplexer u_R1 (
    ._0(AND_r1), ._1(OR_r1), ._2(ADD_r1), ._3(SUB_r1), ._4(SLT_r1), ._5(NOR_r1), .R(R1), .C3(C3), .C2(C2),
    .C1(C1), .C0(C0));
  _6_to_1_multiplexer u_R2 (
    ._0(AND_r2), ._1(OR_r2), ._2(ADD_r2), ._3(SUB_r2), ._4(SLT_r2), ._5(NOR_r2), .R(R2), .C3(C3), .C2(C2),
    .C1(C1), .C0(C0));
  _6_to_1_multiplexer u_R3 (
    ._0(AND_r3), ._1(OR_r3), ._2(ADD_r3), ._3(SUB_r3), ._4(SLT_r3), ._5(NOR_r3), .R(R3), .C3(C3), .C2(C2),
    .C1(C1), .C0(C0));
  _6_to_1_multiplexer u_Overflow (
    ._0(Should_stay_Zero), ._1(Should_stay_Zero), ._2(ADD_overflow), ._3(SUB_overflow),
    ._4(Should_stay_Zero), ._5(Should_stay_Zero), .R(OVERFLOW), .C3(C3), .C2(C2), .C1(C1), .C0(C0));
  not not_2 (not_2_out, R0);
  not not_3 (not_3_out, R1);
  not not_4 (not_4_out, R2);
  not not_5 (not_5_out, R3);
  and and_2 (ZERO, not_2_out, not_3_out, not_4_out, not_5_out);
endmodule

module tester (
  input  Always_0,
  input  C0,
  input  C1,
  input  C2,
  input  C3,
  input  A0,
  input  B0,
  input  A1,
  input  B1,
  input  A2,
  input  B2,
  input  A3,
  input  B3,
  output R0,
  output R1,
  output R2,
  output R3,
  output OVERFLOW,
  output ZERO
);

  ALU alu_1 (
    .C0(C0), .C1(C1), .C2(C2), .C3(C3), .A0(A0), .B0(B0), .A1(A1), .B1(B1), .A2(A2), .B2(B2), .A3(A3),
    .B3(B3), .Should_stay_Zero(Always_0), .R0(R0), .R1(R1), .R2(R2), .R3(R3), .OVERFLOW(OVERFLOW), .ZERO(ZERO));
endmodule
